// Logisim project alu.circ as structural Verilog: 13 circuits, main circuit main
module main (
  input  [31:0] X,
  input  [31:0] Y,
  input  [3:0] Switch,
  output Signed_Overflow,
  output Equal,
  output [31:0] Result
);

  wire add_1_overflow, sub_1_overflow;
  wire [31:0] add_1_out, addu_1_out, and_1_out, or_1_out, sll_1_out, slt_1_out, sltu_1_out, sra_1_out,
       srl_1_out, sub_1_out, subu_1_out, xor_1_out;

  add add_1 (.X(X), .Y(Y), .out(add_1_out), .overflow(add_1_overflow));
  addu addu_1 (.X(X), .Y(Y), .out(addu_1_out));
  sub sub_1 (.X(X), .Y(Y), .out(sub_1_out), .overflow(sub_1_overflow));
  subu subu_1 (.X(X), .Y(Y), .out(subu_1_out));
  \and  and_1 (.Y(Y), .X(X), .out(and_1_out));
  \or  or_1 (.X(X), .Y(Y), .out(or_1_out));
  \xor  xor_1 (.X(X), .Y(Y), .out(xor_1_out));
  slt slt_1 (.X(X), .Y(Y), .out(slt_1_out));
  sltu sltu_1 (.X(X), .Y(Y), .out(sltu_1_out));
  sll sll_1 (.Y(Y), .X(X), .out(sll_1_out));
  srl srl_1 (.Y(Y), .X(X), .out(srl_1_out));
  sra sra_1 (.Y(Y), .X(X), .out(sra_1_out));
  Multiplexer #(.select(4), .width(32), .enable("false")) multiplexer_1 (
    .in0(add_1_out), .in1(addu_1_out), .in2(sub_1_out), .in3(subu_1_out), .in4(and_1_out), .in5(or_1_out),
    .in6(xor_1_out), .in7(slt_1_out), .in8(sltu_1_out), .in9(sll_1_out), .in10(srl_1_out), .in11(sra_1_out),
    .out(Result), .sel(Switch));  // open: in12, in13, in14, in15
  Comparator #(.width(32)) comparator_1 (.a(X), .b(Y), .eq(Equal));  // open: gt, lt
  Multiplexer #(.select(4), .enable("false")) multiplexer_2 (
    .in0(add_1_overflow), .in1(1'b0), .in2(sub_1_overflow), .in3(1'b0), .in4(1'b0), .in5(1'b0), .in6(1'b0),
    .in7(1'b0), .in8(1'b0), .in9(1'b0), .in10(1'b0), .in11(1'b0), .out(Signed_Overflow), .sel(Switch));  // open: in12, in13, in14, in15

  // Other names for the same wires on the sheet: overflow = Signed_Overflow; S[3:0] = Switch

  // Notes on the sheet:
  //   INPUTS to your circuit
  //   DON'T CHANGE THE LOCATIONS OF THE INPUTS AND OUTPUTS!
  //   OUTPUTS from your circuit
endmodule

module add (
  input  [31:0] X,
  input  [31:0] Y,
  output [31:0] out,
  output overflow
);

  wire and_1_out, and_2_out, result, result_t, x_t, x_t_t, y_t, y_t_t;

  Comparator #(.width(32)) comparator_1 (.a(X), .b({32{1'b0}}), .gt(x_t), .lt(x_t_t));  // open: eq
  Comparator #(.width(32)) comparator_2 (.a({32{1'b0}}), .b(Y), .gt(y_t), .lt(y_t_t));  // open: eq
  and and_1 (and_1_out, x_t, result_t, y_t_t);
  and and_2 (and_2_out, x_t_t, result, y_t);
  Adder #(.width(32)) adder_1 (.a(X), .b(Y), .out(out));  // open: cin, cout
  or or_1 (overflow, and_1_out, and_2_out);
  Comparator #(.width(32)) comparator_3 (.a(out), .b({32{1'b0}}), .gt(result), .lt(result_t));  // open: eq
endmodule

module addu (
  input  [31:0] X,
  input  [31:0] Y,
  output [31:0] out
);

  Adder #(.width(32)) adder_1 (.a(X), .b(Y), .out(out));  // open: cin, cout
endmodule

module sub (
  input  [31:0] X,
  input  [31:0] Y,
  output [31:0] out,
  output overflow
);

  wire and_1_out, and_2_out, result, result_t, x_t, x_t_t, y_t, y_t_t;

  Comparator #(.width(32)) comparator_1 (.a(X), .b({32{1'b0}}), .gt(x_t), .lt(x_t_t));  // open: eq
  Comparator #(.width(32)) comparator_2 (.a({32{1'b0}}), .b(Y), .gt(y_t_t), .lt(y_t));  // open: eq
  and and_1 (and_1_out, x_t, result_t, y_t_t);
  and and_2 (and_2_out, x_t_t, result, y_t);
  Subtractor #(.width(32)) subtractor_1 (.a(X), .b(Y), .out(out));  // open: bin, bout
  or or_1 (overflow, and_1_out, and_2_out);
  Comparator #(.width(32)) comparator_3 (.a(out), .b({32{1'b0}}), .gt(result), .lt(result_t));  // open: eq
endmodule

module subu (
  input  [31:0] X,
  input  [31:0] Y,
  output [31:0] out
);

  Subtractor #(.width(32)) subtractor_1 (.a(X), .b(Y), .out(out));  // open: bin, bout
endmodule

module \and  (
  input  [31:0] Y,
  input  [31:0] X,
  output [31:0] out
);

  assign out = Y & X;  // AND_Gate and_1, 32 bits wide
endmodule

module \or  (
  input  [31:0] X,
  input  [31:0] Y,
  output [31:0] out
);

  assign out = X | Y;  // OR_Gate or_1, 32 bits wide
endmodule

module \xor  (
  input  [31:0] X,
  input  [31:0] Y,
  output [31:0] out
);

  assign out = X ^ Y;  // XOR_Gate xor_1, 32 bits wide
endmodule

module slt (
  input  [31:0] X,
  input  [31:0] Y,
  output [31:0] out
);

  wire comparator_1_lt;

  Comparator #(.width(32)) comparator_1 (.a(X), .b(Y), .lt(comparator_1_lt));  // open: gt, eq
  assign out = {{31{1'b0}}, comparator_1_lt};  // Bit_Extender bit_extender_1
endmodule

module sltu (
  input  [31:0] X,
  input  [31:0] Y,
  output [31:0] out
);

  wire comparator_1_lt;

  Comparator #(.width(32), .mode("unsigned")) comparator_1 (.a(X), .b(Y), .lt(comparator_1_lt));  // open: gt, eq
  assign out = {{31{1'b0}}, comparator_1_lt};  // Bit_Extender bit_extender_1
endmodule

module sll (
  input  [31:0] Y,
  input  [31:0] X,
  output [31:0] out
);

  wire [4:0] bit_extender_1_out;

  Bit_Extender #(.in_width(32), .out_width(5)) bit_extender_1 (.in(X), .out(bit_extender_1_out));
  Shifter #(.width(32)) shifter_1 (.in(Y), .\dist (bit_extender_1_out), .out(out));
endmodule

module srl (
  input  [31:0] Y,
  input  [31:0] X,
  output [31:0] out
);

  wire [4:0] bit_extender_1_out;

  Bit_Extender #(.in_width(32), .out_width(5)) bit_extender_1 (.in(X), .out(bit_extender_1_out));
  Shifter #(.width(32), .shift("lr")) shifter_1 (.in(Y), .\dist (bit_extender_1_out), .out(out));
endmodule

module sra (
  input  [31:0] Y,
  input  [31:0] X,
  output [31:0] out
);

  wire [4:0] bit_extender_1_out;

  Bit_Extender #(.in_width(32), .out_width(5)) bit_extender_1 (.in(X), .out(bit_extender_1_out));
  Shifter #(.width(32), .shift("ar")) shifter_1 (.in(Y), .\dist (bit_extender_1_out), .out(out));
endmodule
